# Fritzing sketch MicroRibbon (saved by Fritzing 1.0.2b)
circuit board: 5.58674cm x 3.48583cm
breadboards: 1

parts:
  J1 = double row female pin header, 24 pins [form="♀ (female)"]
  J2 = double row female pin header, 24 pins [form="♀ (female)"]
  U1 = 3.5mm Audio Jack [package=audio-jack]
  R1 = Resistor [tolerance=±5% power=0.25W resistance=220k package=THT]
  R2 = Rotary Potentiometer (Small) [maximum_resistance=10kΩ knob_status=50% power=0.5W package=THT]
  C1 = Ceramic Capacitor [capacitance=100nF voltage=35V package="200 mil [THT, multilayer]"]
  Ribbon = female pin header, 3 pins [form="♀ (female)"]

nets:
  N1: J1.pin1, J1.pin24
  N2: J1.pin2, J1.pin23
  N3: J1.pin3, J1.pin22
  N4: J1.pin4, J1.pin21
  N5: J1.pin5, J1.pin20
  N6: J1.pin6, J1.pin19
  N7: J1.pin7, J1.pin18, U1.LEFT
  N8: J1.pin8, J1.pin17, U1.RIGHT
  N9: J1.pin9, J1.pin16
  N10: J1.pin10, J1.pin15, U1.SLEEVE, R2.leg1
  N11: J1.pin11, J1.pin14
  N12: J1.pin12, J1.pin13
  N13: J2.pin1, J2.pin24
  N14: J2.pin2, J2.pin23
  N15: J2.pin3, J2.pin22
  N16: J2.pin4, J2.pin21
  N17: J2.pin5, J2.pin20, R1.Pin_1, C1.1, Ribbon.pin2
  N18: J2.pin6, J2.pin19, R2.wiper
  N19: J2.pin7, J2.pin18
  N20: J2.pin8, J2.pin17
  N21: J2.pin9, J2.pin16, R2.leg2, Ribbon.pin1
  N22: J2.pin10, J2.pin15
  N23: J2.pin11, J2.pin14, R1.Pin_0, C1.0, Ribbon.pin3
  N24: J2.pin12, J2.pin13

notes:
  GND
  RAW
  6-16 VIN
  V+
  In
  A0
  KRAMER 2024
  3
